// Logisim project t.circ as structural Verilog
module a1 (
  input  x,
  input  y,
  input  z,
  input  w,
  output f
);

  wire and_1_out, and_2_out, and_3_out, not_1_out, not_2_out, not_3_out, not_4_out, not_5_out, not_6_out,
       not_7_out, not_8_out, not_9_out, not_10_out, not_11_out, not_12_out, not_13_out, or_1_out, or_2_out,
       or_3_out, or_4_out, or_5_out, or_6_out, or_7_out, or_8_out, or_9_out, or_10_out, or_11_out, or_12_out,
       or_13_out, or_14_out, or_15_out;

  or or_1 (or_1_out, x, not_1_out);
  not not_1 (not_1_out, y);
  or or_2 (or_2_out, z, w);
  or or_3 (or_3_out, x, not_2_out);
  not not_2 (not_2_out, y);
  not not_3 (not_3_out, z);
  or or_4 (or_4_out, not_3_out, w);
  not not_4 (not_4_out, y);
  not not_5 (not_5_out, z);
  not not_6 (not_6_out, w);
  not not_7 (not_7_out, x);
  not not_8 (not_8_out, y);
  not not_9 (not_9_out, w);
  not not_10 (not_10_out, x);
  not not_11 (not_11_out, y);
  not not_12 (not_12_out, z);
  not not_13 (not_13_out, w);
  or or_5 (or_5_out, or_1_out, or_2_out);
  or or_6 (or_6_out, or_3_out, or_4_out);
  or or_7 (or_7_out, x, not_4_out);
  or or_8 (or_8_out, not_5_out, not_6_out);
  or or_9 (or_9_out, not_7_out, not_8_out);
  or or_10 (or_10_out, z, not_9_out);
  or or_11 (or_11_out, not_10_out, not_11_out);
  or or_12 (or_12_out, not_12_out, not_13_out);
  and and_1 (and_1_out, or_5_out, or_6_out);
  or or_13 (or_13_out, or_7_out, or_8_out);
  or or_14 (or_14_out, or_9_out, or_10_out);
  or or_15 (or_15_out, or_11_out, or_12_out);
  and and_2 (and_2_out, and_1_out, or_13_out);
  and and_3 (and_3_out, or_14_out, or_15_out);
  and and_4 (f, and_2_out, and_3_out);
endmodule

module a2 (
  input  x,
  input  y,
  input  z,
  input  w,
  output f
);

  wire and_1_out, and_2_out, and_3_out, not_1_out, not_2_out, not_3_out, not_4_out, or_1_out;

  not not_1 (not_1_out, x);
  and and_1 (and_1_out, not_1_out, not_2_out);
  not not_2 (not_2_out, z);
  not not_3 (not_3_out, y);
  and and_2 (and_2_out, and_1_out, w);
  not not_4 (not_4_out, w);
  or or_1 (or_1_out, not_3_out, and_2_out);
  and and_3 (and_3_out, x, not_4_out);
  or or_2 (f, or_1_out, and_3_out);
endmodule

module a3 (
  input  x,
  input  y,
  input  z,
  input  w,
  output f
);

  wire and_1_out, and_2_out, and_3_out, and_4_out, not_1_out, not_2_out, not_3_out, not_4_out, not_5_out,
       not_6_out, or_1_out, or_2_out;

  not not_1 (not_1_out, y);
  not not_2 (not_2_out, x);
  and and_1 (and_1_out, not_2_out, not_3_out);
  not not_3 (not_3_out, z);
  not not_4 (not_4_out, x);
  and and_2 (and_2_out, not_4_out, not_5_out);
  not not_5 (not_5_out, y);
  or or_1 (or_1_out, not_1_out, and_1_out);
  not not_6 (not_6_out, w);
  or or_2 (or_2_out, x, and_2_out);
  and and_3 (and_3_out, w, or_1_out);
  and and_4 (and_4_out, not_6_out, or_2_out);
  or or_3 (f, and_3_out, and_4_out);
endmodule

module a4 (
  input  x,
  input  y,
  input  z,
  input  w,
  output f
);

  wire and_1_out, and_2_out, and_3_out, and_4_out, and_5_out, and_6_out, and_7_out, xor_1_out, xor_2_out,
       xor_3_out, xor_4_out;

  and and_1 (and_1_out, y, z);
  and and_2 (and_2_out, x, y);
  and and_3 (and_3_out, and_1_out, w);
  and and_4 (and_4_out, x, y);
  and and_5 (and_5_out, z, w);
  xor xor_1 (xor_1_out, 1'b1, y);
  and and_6 (and_6_out, y, w);
  xor xor_2 (xor_2_out, and_2_out, and_3_out);
  and and_7 (and_7_out, and_4_out, and_5_out);
  xor xor_3 (xor_3_out, xor_1_out, and_6_out);
  xor xor_4 (xor_4_out, xor_2_out, and_7_out);
  xor xor_5 (f, xor_3_out, xor_4_out);
endmodule

module a5 (
  input  x,
  input  y,
  input  z,
  input  w,
  output f
);

  wire and_1_out, and_2_out, and_3_out, not_1_out, not_2_out, not_3_out, not_4_out, or_1_out;

  not not_1 (not_1_out, y);
  not not_2 (not_2_out, w);
  and and_1 (and_1_out, not_2_out, x);
  and and_2 (and_2_out, w, not_3_out);
  not not_3 (not_3_out, x);
  not not_4 (not_4_out, z);
  or or_1 (or_1_out, not_1_out, and_1_out);
  and and_3 (and_3_out, and_2_out, not_4_out);
  or or_2 (f, or_1_out, and_3_out);
endmodule
